// Logisim project aois-laba-5.circ as structural Verilog: 1 circuit, main circuit main
module main (
  input  in_1
);

  wire and_1_out, and_2_out, and_3_out, clock_1_out;
  wire [2:0] TD_q;

  and and_1 (and_1_out, in_1, TD_q[2], TD_q[1], TD_q[0]);
  and and_2 (and_2_out, in_1, TD_q[1], TD_q[0]);
  and and_3 (and_3_out, in_1, TD_q[0]);
  Clock #(.lowDuration(14)) clock_1 (.out(clock_1_out));
  T_Flip_Flop TA (.clk(clock_1_out), .T(and_1_out));  // open: Q, Qn, preset, reset, en
  T_Flip_Flop TB (.clk(clock_1_out), .T(and_2_out), .Q(TD_q[2]));  // open: Qn, preset, reset, en
  T_Flip_Flop TC (.clk(clock_1_out), .T(and_3_out), .Q(TD_q[1]));  // open: Qn, preset, reset, en
  T_Flip_Flop TD (.clk(clock_1_out), .T(in_1), .Q(TD_q[0]));  // open: Qn, preset, reset, en
  // Probe on TD_q
endmodule
